// Logisim project 74IC.circ as structural Verilog: 1 circuit, main circuit 74283
module _74283 (
  input  B4,
  input  VCC,
  input  GND,
  input  A4,
  input  B3,
  input  A3,
  input  B2,
  input  A2,
  input  B1,
  input  A1,
  input  C0,
  output C4,
  output Z4,
  output Z3,
  output Z2,
  output Z1
);

  wire and_1_out, and_2_out, nand_1_out, nand_2_out, nand_3_out, nand_4_out, nand_5_out, nand_6_out,
       nand_7_out, nand_8_out, nand_9_out, nand_10_out, nand_11_out, nand_12_out, nand_13_out, nand_14_out,
       nand_15_out, nand_16_out, nand_17_out, nand_18_out, nand_19_out, nand_20_out, nor_1_out, nor_2_out,
       nor_3_out, nor_4_out, nor_5_out, nor_6_out, nor_7_out, nor_8_out, nor_9_out, nor_10_out, not_1_out,
       not_2_out, not_3_out, not_4_out, not_5_out, not_6_out, not_7_out, not_8_out, not_9_out, not_10_out,
       not_11_out, not_12_out, not_13_out, not_14_out, not_15_out, not_16_out, not_17_out, not_18_out,
       not_19_out, not_20_out, not_21_out, not_22_out, not_23_out, not_24_out, not_25_out, not_26_out,
       not_27_out, not_28_out, not_29_out, not_30_out, not_31_out, xor_1_out, xor_2_out, xor_3_out, xor_4_out;

  not not_1 (not_1_out, B4);
  not not_2 (not_2_out, A4);
  not not_3 (not_3_out, B3);
  not not_4 (not_4_out, A3);
  not not_5 (not_5_out, B2);
  not not_6 (not_6_out, A2);
  not not_7 (not_7_out, B1);
  not not_8 (not_8_out, A1);
  nor nor_1 (nor_1_out, not_1_out, not_2_out);
  nand nand_1 (nand_1_out, not_1_out, not_2_out);
  nor nor_2 (nor_2_out, not_3_out, not_4_out);
  nand nand_2 (nand_2_out, not_3_out, not_4_out);
  nor nor_3 (nor_3_out, not_5_out, not_6_out);
  nand nand_3 (nand_3_out, not_5_out, not_6_out);
  nor nor_4 (nor_4_out, not_7_out, not_8_out);
  nand nand_4 (nand_4_out, not_7_out, not_8_out);
  not not_9 (not_9_out, nor_1_out);
  not not_10 (not_10_out, nand_1_out);
  nor nor_5 (nor_5_out, nor_1_out, nor_2_out);
  not not_11 (not_11_out, nor_2_out);
  not not_12 (not_12_out, nand_2_out);
  not not_13 (not_13_out, nor_3_out);
  not not_14 (not_14_out, nand_3_out);
  nor nor_6 (nor_6_out, nor_3_out, nor_4_out);
  not not_15 (not_15_out, nor_4_out);
  not not_16 (not_16_out, nand_4_out);
  not not_17 (not_17_out, C0);
  and and_1 (and_1_out, not_12_out, not_9_out);
  nand nand_5 (nand_5_out, not_14_out, not_9_out, not_11_out);
  nand nand_6 (nand_6_out, not_16_out, nor_5_out, not_13_out);
  nand nand_7 (nand_7_out, nor_5_out, not_13_out, not_15_out);
  not not_18 (not_18_out, not_17_out);
  not not_19 (not_19_out, not_10_out);
  and and_2 (and_2_out, not_14_out, not_11_out);
  nand nand_8 (nand_8_out, not_16_out, not_11_out, not_13_out);
  nand nand_9 (nand_9_out, not_11_out, nor_6_out, not_17_out);
  not not_20 (not_20_out, not_12_out);
  not not_21 (not_21_out, not_14_out);
  nand nand_10 (nand_10_out, not_16_out, not_13_out);
  nand nand_11 (nand_11_out, nor_6_out, not_17_out);
  not not_22 (not_22_out, not_14_out);
  not not_23 (not_23_out, not_16_out);
  nand nand_12 (nand_12_out, not_15_out, not_17_out);
  not not_24 (not_24_out, not_16_out);
  not not_25 (not_25_out, not_17_out);
  nor nor_7 (nor_7_out, not_10_out, and_1_out);
  nor nor_8 (nor_8_out, not_12_out, and_2_out);
  nand nand_13 (nand_13_out, nor_7_out, nand_5_out, nand_6_out);
  nor nor_9 (nor_9_out, nand_7_out, not_18_out);
  nand nand_14 (nand_14_out, not_9_out, not_19_out);
  nand nand_15 (nand_15_out, nor_8_out, nand_8_out, nand_9_out);
  nand nand_16 (nand_16_out, not_11_out, not_20_out);
  nand nand_17 (nand_17_out, not_21_out, nand_10_out, nand_11_out);
  nand nand_18 (nand_18_out, not_13_out, not_22_out);
  nand nand_19 (nand_19_out, not_23_out, nand_12_out);
  nand nand_20 (nand_20_out, not_15_out, not_24_out);
  not not_26 (not_26_out, not_25_out);
  not not_27 (not_27_out, nor_10_out);
  nor nor_10 (nor_10_out, nand_13_out, nor_9_out);
  xor xor_1 (xor_1_out, nand_14_out, nand_15_out);
  not not_28 (not_28_out, xor_1_out);
  not not_29 (not_29_out, xor_2_out);
  xor xor_2 (xor_2_out, nand_16_out, nand_17_out);
  xor xor_3 (xor_3_out, nand_18_out, nand_19_out);
  not not_30 (not_30_out, xor_3_out);
  xor xor_4 (xor_4_out, nand_20_out, not_26_out);
  not not_31 (not_31_out, xor_4_out);
  not not_32 (C4, not_27_out);
  not not_33 (Z4, not_28_out);
  not not_34 (Z3, not_29_out);
  not not_35 (Z2, not_30_out);
  not not_36 (Z1, not_31_out);
endmodule
